// Logisim project hw5q14.circ as structural Verilog: 1 circuit, main circuit main
module main (
  input  X,
  input  Y,
  input  Z,
  output S
);

  wire and_1_out, and_2_out, not_1_out, xnor_1_out, xor_1_out;

  not not_1 (not_1_out, Z);
  xnor xnor_1 (xnor_1_out, X, Y);
  xor xor_1 (xor_1_out, X, Y);
  and and_1 (and_1_out, xnor_1_out, Z);
  and and_2 (and_2_out, xor_1_out, not_1_out);
  or or_1 (S, and_1_out, and_2_out);
endmodule
