// Logisim project hw5q21.circ as structural Verilog: 1 circuit, main circuit main
module main (
  input  in_1,
  input  in_2,
  output out_3,
  output out_4,
  output out_5
);

  wire adder_1_cout, clock_1_out;

  Adder #(.width(1)) adder_1 (.a(in_1), .b(in_2), .out(out_3), .cin(out_4), .cout(adder_1_cout));
  not not_1 (out_5, adder_1_cout);
  Clock clock_1 (.out(clock_1_out));
  D_Flip_Flop d_ff_1 (.clk(clock_1_out), .D(out_5), .Q(out_4));  // open: Qn, preset, en, reset
endmodule
