// Logisim project hw5q31.circ as structural Verilog: 1 circuit, main circuit main
module main (
  input  X,
  input  Y,
  output A,
  output B,
  output Z
);

  wire and_1_out, and_2_out, and_3_out, and_4_out, and_5_out, and_6_out, clock_1_out, not_1_out, not_2_out,
       or_1_out, or_3_out, or_4_out;

  not not_1 (not_1_out, X);
  not not_2 (not_2_out, Y);
  and and_1 (and_1_out, B, Y);
  and and_2 (and_2_out, Y, not_1_out);
  or or_1 (or_1_out, and_2_out, and_1_out);
  Clock clock_1 (.out(clock_1_out));
  and and_3 (and_3_out, B, not_2_out);
  and and_4 (and_4_out, Y, X);
  and and_5 (and_5_out, not_2_out, A);
  and and_6 (and_6_out, B, X);
  or or_2 (Z, and_2_out, X);
  D_Flip_Flop d_ff_1 (.clk(or_1_out), .D(clock_1_out), .Q(A));  // open: Qn, preset, en, reset
  or or_3 (or_3_out, and_3_out, and_4_out);
  or or_4 (or_4_out, and_5_out, and_6_out);
  J_K_Flip_Flop j_k_ff_1 (.J(or_3_out), .clk(clock_1_out), .K(or_4_out), .Q(B));  // open: Qn, preset, en, reset
endmodule
