// Logisim project hw5q44.circ as structural Verilog: 1 circuit, main circuit main
module main (
  input  A,
  input  B,
  input  C,
  output out_4,
  output out_5,
  output out_6
);

  wire and_1_out, clock_1_out, not_1_out, not_3_out, or_1_out, xnor_1_out;

  not not_1 (not_1_out, A);
  // NOT_Gate not_2 has open pins: in=B, out=open
  not not_3 (not_3_out, C);
  and and_1 (and_1_out, A, not_3_out);
  Clock clock_1 (.out(clock_1_out));
  or or_1 (or_1_out, not_1_out, and_1_out);
  xnor xnor_1 (xnor_1_out, A, B);
  J_K_Flip_Flop j_k_ff_1 (.J(not_3_out), .clk(clock_1_out), .K(B), .Q(out_4));  // open: Qn, preset, en, reset
  J_K_Flip_Flop j_k_ff_2 (.J(or_1_out), .clk(clock_1_out), .K(or_1_out), .Q(out_5));  // open: Qn, preset, en, reset
  J_K_Flip_Flop j_k_ff_3 (.J(xnor_1_out), .clk(clock_1_out), .K(B), .Q(out_6));  // open: Qn, preset, en, reset

  // Notes on the sheet:
  //   A
  //   B
  //   C
endmodule
