// Logisim project nguyew2_hw4.circ as structural Verilog: 1 circuit, main circuit main
module main (
  input  X,
  input  Y,
  input  Z,
  output A,
  output B,
  output C
);

  wire and_1_out, and_2_out, and_3_out, and_4_out, nand_1_out, nand_2_out, not_1_out, not_2_out, not_3_out;

  not not_1 (not_1_out, X);
  not not_2 (not_2_out, Z);
  not not_3 (not_3_out, Y);
  and and_1 (and_1_out, X, Z, not_3_out);
  and and_2 (and_2_out, X, Z, Y);
  nand nand_1 (nand_1_out, not_2_out, not_3_out);
  nand nand_2 (nand_2_out, not_1_out, not_3_out);
  and and_3 (and_3_out, not_1_out, Z);
  and and_4 (and_4_out, X, not_2_out);
  or or_1 (A, and_1_out, Y);
  or or_2 (B, and_2_out, nand_1_out, nand_2_out);
  or or_3 (C, and_3_out, and_4_out);
endmodule
